// Digital circuit TTL640x480.dig as structural Verilog
module TTL640x480 (
  input  CLK,
  output HBLANK,
  output nHBLANK,
  output HSYNC,
  output nHSYNC,
  output VSYNC,
  output nVSYNC,
  output VBLANK,
  output nVBLANK,
  output [9:0] VCNT,
  output [9:0] HCNT
);

  wire _1_frame_out, _1_px_out, _1_row_out, _50_px_out, _50_rows_out, _7400_1_pin3, _7400_1_pin9,
       _7400_2_pin1, _7400_2_pin5, _7400_2_pin9, _7404_1_pin1, _7404_1_pin2, _7404_1_pin3, _7404_1_pin4,
       _7427_1_pin6, _74393_2_pin6, _74393_3_pin8, _74393_3_pin9, and_1_out, d_ff_1_q, d_ff_2_q, d_ff_3_q,
       d_ff_4_q, H_CLK, monoflop_1_q, monoflop_2_q, monoflop_3_q, monoflop_4_q, or_1_out, or_2_out,
       pulldown_2_out;

  _7404 _7404_1 (
    .pin1(_7404_1_pin1), .pin2(_7404_1_pin2), .pin3(_7404_1_pin3), .pin4(_7404_1_pin4), .pin5(1'b0),
    .pin7(1'b0), .pin9(1'b1), .pin11(1'b1), .pin13(1'b1), .pin14(1'b1));  // open: pin6, pin8, pin10, pin12
  assign H_CLK = CLK ? CLK : 1'bz;  // Driver driver_1
  PullDown pulldown_1 (.out(H_CLK));
  _74393 _74393_1 (
    .pin1(H_CLK), .pin2(_7404_1_pin2), .pin3(HCNT[0]), .pin4(HCNT[1]), .pin5(HCNT[2]), .pin7(1'b0),
    .pin8(HCNT[6]), .pin9(HCNT[5]), .pin10(HCNT[4]), .pin11(HCNT[3]), .pin12(_7404_1_pin2), .pin13(HCNT[2]),
    .pin14(1'b1));  // open: pin6
  _74393 _74393_2 (
    .pin1(HCNT[6]), .pin2(_7404_1_pin2), .pin3(HCNT[7]), .pin4(HCNT[8]), .pin5(HCNT[9]),
    .pin6(_74393_2_pin6), .pin7(1'b0), .pin8(VCNT[3]), .pin9(VCNT[2]), .pin10(VCNT[1]), .pin11(VCNT[0]),
    .pin12(_7404_1_pin4), .pin13(HSYNC), .pin14(1'b1));
  _74393 _74393_3 (
    .pin1(VCNT[3]), .pin2(_7404_1_pin4), .pin3(VCNT[4]), .pin4(VCNT[5]), .pin5(VCNT[6]), .pin6(VCNT[7]),
    .pin7(1'b0), .pin8(_74393_3_pin8), .pin9(_74393_3_pin9), .pin10(VCNT[9]), .pin11(VCNT[8]),
    .pin12(_7404_1_pin4), .pin13(VCNT[7]), .pin14(1'b1));
  _7400 _7400_1 (
    .pin1(HCNT[6]), .pin2(HCNT[6]), .pin3(_7400_1_pin3), .pin4(nVSYNC), .pin5(nVSYNC), .pin6(VSYNC),
    .pin7(1'b0), .pin8(VBLANK), .pin9(_7400_1_pin9), .pin10(nVBLANK), .pin11(nVBLANK), .pin12(VBLANK),
    .pin13(_7404_1_pin3), .pin14(1'b1));
  _7400 _7400_2 (
    .pin1(_7400_2_pin1), .pin2(nHSYNC), .pin3(HSYNC), .pin4(HSYNC), .pin5(_7400_2_pin5), .pin6(nHSYNC),
    .pin7(1'b0), .pin8(HBLANK), .pin9(_7400_2_pin9), .pin10(nHBLANK), .pin11(nHBLANK), .pin12(HBLANK),
    .pin13(_7404_1_pin1), .pin14(1'b1));
  _7420 _7420_1 (
    .pin1(VCNT[9]), .pin2(VCNT[3]), .pin4(VCNT[2]), .pin5(VCNT[0]), .pin6(_7404_1_pin3), .pin7(1'b0),
    .pin8(_7400_1_pin9), .pin9(VCNT[8]), .pin10(VCNT[7]), .pin12(VCNT[6]), .pin13(VCNT[5]), .pin14(1'b1));  // open: pin3, pin11
  _7420 _7420_2 (
    .pin1(_7400_1_pin3), .pin2(HCNT[7]), .pin4(HCNT[4]), .pin5(HBLANK), .pin6(_7400_2_pin1), .pin7(1'b0),
    .pin8(_7400_2_pin5), .pin9(HBLANK), .pin10(HCNT[4]), .pin12(HCNT[5]), .pin13(HCNT[6]), .pin14(1'b1));  // open: pin3, pin11
  _7427 _7427_1 (
    .pin1(1'b0), .pin2(1'b0), .pin3(VCNT[2]), .pin4(VCNT[4]), .pin5(_7400_1_pin9), .pin6(_7427_1_pin6),
    .pin7(1'b0), .pin9(1'b1), .pin10(1'b1), .pin11(1'b1), .pin13(1'b1), .pin14(1'b1));  // open: pin8, pin12
  _7410 _7410_1 (
    .pin1(HCNT[9]), .pin2(HCNT[7]), .pin3(HBLANK), .pin4(HCNT[5]), .pin5(HCNT[8]), .pin6(_7404_1_pin1),
    .pin7(1'b0), .pin8(nVSYNC), .pin9(_7427_1_pin6), .pin10(VCNT[3]), .pin11(VCNT[1]), .pin12(_7400_2_pin9),
    .pin13(HCNT[7]), .pin14(1'b1));
  Button _1_px (.out(_1_px_out));
  Button _50_px (.out(_50_px_out));
  D_FF d_ff_1 (.D(_50_px_out), .C(pulldown_2_out), .Q(d_ff_1_q));  // open: nQ
  Button _1_row (.out(_1_row_out));
  D_FF d_ff_2 (.D(_1_row_out), .C(pulldown_2_out), .Q(d_ff_2_q));  // open: nQ
  Button _50_rows (.out(_50_rows_out));
  D_FF d_ff_3 (.D(_50_rows_out), .C(pulldown_2_out), .Q(d_ff_3_q));  // open: nQ
  D_FF d_ff_4 (.D(_1_frame_out), .C(pulldown_2_out), .Q(d_ff_4_q));  // open: nQ
  Button _1_frame (.out(_1_frame_out));
  Monoflop #(.timerDelay(49)) monoflop_1 (.C(d_ff_1_q), .R(1'b0), .Q(monoflop_1_q));  // open: nQ
  Monoflop #(.timerDelay(799)) monoflop_2 (.C(d_ff_2_q), .R(1'b0), .Q(monoflop_2_q));  // open: nQ
  Monoflop #(.timerDelay(39999)) monoflop_3 (.C(d_ff_3_q), .R(1'b0), .Q(monoflop_3_q));  // open: nQ
  Monoflop #(.timerDelay(419999)) monoflop_4 (.C(d_ff_4_q), .R(1'b0), .Q(monoflop_4_q));  // open: nQ
  // Probe H_PIXEL on HCNT
  LED led_1 (.in(HBLANK));
  LED led_2 (.in(HSYNC));
  // Probe V_LINE on VCNT
  LED led_3 (.in(VBLANK));
  LED led_4 (.in(VSYNC));
  LED led_5 (.in(pulldown_2_out));
  or or_1 (or_1_out, monoflop_1_q, monoflop_2_q, monoflop_3_q, monoflop_4_q);
  and and_1 (and_1_out, pulldown_2_out, or_1_out);
  PullDown pulldown_2 (.out(pulldown_2_out));
  or or_2 (or_2_out, _1_px_out, and_1_out);
  assign H_CLK = or_2_out ? or_2_out : 1'bz;  // Driver driver_2
  PullDown pulldown_3 (.out(H_CLK));

  // Notes on the sheet:
  //   INV. FOR
  //   CNTR RESETS
  //   IC8
  //   COUNTERS FOR
  //   HORIZONTAL (1.5 chip)
  //   VERTICAL (1.5 chip)
  //   IC1
  //   IC2
  //   IC3
  //   Test implementation of the low chip count VGA generator
  //   from https://github.com/SmallRoomLabs/TTL640x480
  //   (VCLK)
  //   IC9
  //   IC6
  //   VERTICAL SYNC &
  //   BLANKING GENERATION
  //   HORIZONTAL SYNC &
  //   BLANKING GENERATION
  //   IC10
  //   IC4
  //   IC5(diodes)
  //   IC7
  //   CLOCK GENERATOR FOR LOCAL TESTING
  //   Visible area	640 px
  //   Front porch	16 px
  //   Sync pulse	96 px
  //   Back porch	48 px
  //   Whole line	800 px
  //   Visible area	480
  //   Front porch	10
  //   Sync pulse	2
  //   Back porch	33
  //   Whole frame	525
  //   NOTE!  Replace the green 
  //   LED here with a "Clock Input" 
  //   component to use the test 
  //   buttons.
endmodule
