// Digital circuit VGA_TTL640x480.dig as structural Verilog
module VGA_TTL640x480 (
  input  clk
);

  wire t_ff_1_q, ttl640x480_1_p2, ttl640x480_1_p3;
  wire [2:0] multiplexer_1_out, ttl640x480_1_p4_2, ttl640x480_1_p5_2;
  wire [9:0] ttl640x480_1_p4, ttl640x480_1_p5;

  // TTL640x480 ttl640x480_1: pin names not known; wires that end beside it: clk, ttl640x480_1_p2, ttl640x480_1_p3, {ttl640x480_1_p4[9:8], ttl640x480_1_p4_2, ttl640x480_1_p4[4:0]}, {ttl640x480_1_p5[9:8], ttl640x480_1_p5_2, ttl640x480_1_p5[4:0]}
  T_FF #(.withEnable("false")) t_ff_1 (.C(ttl640x480_1_p4[9]), .Q(t_ff_1_q));  // open: nQ
  Multiplexer #(.Bits(3)) multiplexer_1 (
    .sel(t_ff_1_q), .in_0(ttl640x480_1_p4_2), .in_1(ttl640x480_1_p5_2), .out(multiplexer_1_out));
  VGA vga_1 (
    .R(multiplexer_1_out[0]), .G(multiplexer_1_out[1]), .B(multiplexer_1_out[2]), .H(ttl640x480_1_p2),
    .V(ttl640x480_1_p3), .C(clk));

  // Notes on the sheet:
  //   clk: Hz: 2147483647
  //   VERTICAL/LINE
  //   COUNTER
  //   HORIZONTAL/PIXEL
  //   COUNTER
endmodule
