// Logisim project Fourplex.circ as structural Verilog: 2 circuits, main circuit main
module main (
);

  wire clock_1_out, RES, ucode_1_incpc, ucode_1_mop5, undriven;
  wire [2:0] counter_1_q;
  wire [3:0] ACC_q, rom_1_data, rom_1_data_2, ucode_1_mop1;
  wire [11:0] PC_q;

  Button button_1 (.out(RES));
  Counter #(.width(12), .max('hfff)) PC (.Q(PC_q), .clk(ucode_1_incpc));  // open: load, D, count, carry, clr
  Counter #(.width(3), .max('h7), .ongoal("stay")) counter_1 (
    .Q(counter_1_q), .clk(clock_1_out), .clr(RES));  // open: load, D, count, carry
  Clock clock_1 (.out(clock_1_out));
  ROM #(.addrWidth(12)) rom_1 (.addr(PC_q), .data({rom_1_data_2, rom_1_data}), .sel(undriven));
  // Probe on counter_1_q
  Register #(.width(4)) ACC (.D(rom_1_data_2), .Q(ACC_q), .clk(ucode_1_mop5));  // open: en, clr
  ucode ucode_1 (
    .cycle(counter_1_q), .op(rom_1_data), .incpc(ucode_1_incpc), .mop1(ucode_1_mop1[0]),
    .mop2(ucode_1_mop1[1]), .mop3(ucode_1_mop1[2]), .mop4(ucode_1_mop1[3]), .mop5(ucode_1_mop5));  // open: in0, in1, in2, in3, in4, in5, in6, in7, in8, in9, in10, in11, mop6, mop7, mop8, mop9, mop10, mop11, mop12, mop13, mop14, mop15
  Register #(.width(4)) register_1 (.D(rom_1_data_2));  // open: en, Q, clk, clr
  Register #(.width(4)) register_2 (.D(rom_1_data_2));  // open: en, Q, clk, clr
  Register #(.width(4)) register_3 ();  // open: D, en, Q, clk, clr
  Register #(.width(4)) register_4 ();  // open: D, en, Q, clk, clr
  Decoder #(.select(4)) decoder_1 (.sel(ucode_1_mop1));  // open: out0, out1, out2, out3, out4, out5, out6, out7, out8, out9, out10, out11, out12, out13, out14, out15, en

  // Notes on the sheet:
  //   0=LDI Load Accumulator Immediate
  //   contents of rom_1 (hex, n*v repeats v):
  //   6 f 1 5
endmodule

module ucode (
  input  in0,
  input  in1,
  input  in2,
  input  in3,
  input  in4,
  input  in5,
  input  in6,
  input  in7,
  input  in8,
  input  in9,
  input  in10,
  input  in11,
  input  [2:0] cycle,
  input  [3:0] op,
  output incpc,
  output mop1,
  output mop2,
  output mop3,
  output mop4,
  output mop5,
  output mop6,
  output mop7,
  output mop8,
  output mop9,
  output mop10,
  output mop11,
  output mop12,
  output mop13,
  output mop14,
  output mop15
);

  ROM #(.addrWidth(19), .dataWidth(16)) rom_1 (
    .addr({op, cycle, in11, in10, in9, in8, in7, in6, in5, in4, in3, in2, in1, in0}),
    .data({mop15, mop14, mop13, mop12, mop11, mop10, mop9, mop8, mop7, mop6, mop5, mop4, mop3, mop2, mop1, incpc}),
    .sel(1'b1));
endmodule
