// Logisim project TTL640x480.circ as structural Verilog: 1 circuit, main circuit main
module main (
  output HSYNC,
  output nHSYNC,
  output HBLANK,
  output nHBLANK,
  output nVSYNC,
  output VBLANK,
  output nVBLANK
);

  wire A1_out, A2_out, C1_out, C2_out, clock_1_out, D3_out, E1_out, E2_out, not_1_out, not_2_out, X_out;
  wire [2:0] counter_1_q;
  wire [6:0] counter_1_q_2;
  wire [9:0] counter_2_q;

  // Probe on counter_1_q
  // Probe on counter_1_q_2
  // Probe on {counter_1_q_2, counter_1_q}
  // Probe on counter_2_q
  Counter #(.width(10), .max('h3ff)) counter_1 (
    .Q({counter_1_q_2, counter_1_q}), .clk(clock_1_out), .clr(not_1_out));  // open: load, D, count, carry
  not not_1 (not_1_out, C1_out);
  Clock clock_1 (.out(clock_1_out));
  Counter #(.width(10), .max('h3ff)) counter_2 (
    .Q(counter_2_q), .clk(clock_1_out), .clr(not_2_out));  // open: load, D, count, carry
  not not_2 (not_2_out, E2_out);
  nand C1 (C1_out, counter_1_q_2[2], counter_1_q_2[5], HBLANK);
  nand D3 (D3_out, counter_1_q_2[3], counter_1_q_2[3]);
  nand A1 (A1_out, D3_out, counter_1_q_2[4], counter_1_q_2[1], HBLANK);
  nand A2 (A2_out, HBLANK, counter_1_q_2[1], counter_1_q_2[2], counter_1_q_2[3]);
  nand C2 (C2_out, counter_1_q_2[6], counter_1_q_2[4], counter_1_q_2[4]);
  nand E1 (E1_out, counter_2_q[8], counter_2_q[7], counter_2_q[6], counter_2_q[5]);
  nand E2 (E2_out, counter_2_q[9], counter_2_q[3], counter_2_q[2], counter_2_q[0]);
  nand B1 (HSYNC, A1_out, nHSYNC);
  nand B2 (nHSYNC, HSYNC, A2_out);
  nand B3 (HBLANK, C2_out, nHBLANK);
  nand B4 (nHBLANK, HBLANK, C1_out);
  nor X (X_out, counter_2_q[4], counter_2_q[2], E1_out);
  nand C3 (nVSYNC, X_out, counter_2_q[3], counter_2_q[1]);
  nand D1 (VBLANK, E1_out, nVBLANK);
  nand D2 (nVBLANK, VBLANK, E2_out);

  // Notes on the sheet:
  //   by Mats.Engstrom@gmail.com
  //   Counter implemented
  //   by 1.5 pcs of 74393
  //   Counter implemented
  //   by 1.5 pcs of 74393
  //   VGA 640x480 @ 60Hz timing generator
  //   (X implemented using three diodes,
  //   a pulldown resistor and D4)
endmodule
